# Fritzing sketch Superprosjekt (saved by Fritzing 0.9.3b)
breadboards: 3

parts:
  hc-sr1 = hc-sr04
  hc-sr2 = hc-sr04

nets:
  VCC: hc-sr1.VCC, hc-sr2.VCC
  N1: hc-sr1.Trig, hc-sr2.Trig
  GND: hc-sr1.GND, hc-sr2.GND

notes:
  Disse går til Bluetooth
  Koblet til Zumo-roboten
  Teipet sammen
